// Logisim project porta 1a.circ as structural Verilog: 2 circuits, main circuit main
module main (
  input  in_1,
  input  in_2,
  output out_3
);

  wire not_1_out, not_2_out, or_1_out;

  not not_1 (not_1_out, in_1);
  not not_2 (not_2_out, in_2);
  or or_1 (or_1_out, not_1_out, not_2_out);
  not not_3 (out_3, or_1_out);
endmodule

module porta_1a (
  input  a,
  input  b,
  output x
);

  wire not_1_out, not_2_out;

  not not_1 (not_1_out, a);
  not not_2 (not_2_out, b);
  nor nor_1 (x, not_1_out, not_2_out);
endmodule
