// Logisim project porta 2a.circ as structural Verilog: 2 circuits, main circuit main
module main (
);

  PORTA porta_1 ();  // open: A, B, C, X
endmodule

module PORTA (
  input  A,
  input  B,
  input  C,
  output X
);

  wire and_1_out, and_2_out, and_3_out;

  and and_1 (and_1_out, B, C);
  and and_2 (and_2_out, A, C);
  and and_3 (and_3_out, A, B);
  or or_1 (X, and_1_out, and_2_out, and_3_out);
endmodule
